# Fritzing sketch Terminator (saved by Fritzing 0.9.2b)

parts:
  U1 = TRANSCHIPTC5747 [package=camera_sfv24r-2st_2]
  U6 = LIPO-7800mAh
  Часть1 = Arduino Nano (Rev3.0) (ICSP)
  J1 = Basic Servo
  Creator_CI20_v2a1 = Creator CI20 v2a

nets:
  N1: U1.AVDD28, Creator_CI20_v2a1.USB
  VIN: U6.+, Часть1.D0/RX, Часть1.RESET, Часть1.GND, Часть1.VIN, Creator_CI20_v2a1.TX, Creator_CI20_v2a1.Vin
  GND: U6.-, J1.gnd, Creator_CI20_v2a1.GND
  N2: Часть1.D1/TX, Creator_CI20_v2a1.RX

custom parts:
  LIPO-7800mAh: 110mAh Lipo-battery
  Creator CI20 v2a: Creator CI20 v2a from imagination technology
